# Fritzing sketch Fritzing_Sketch (saved by Fritzing 0.9.2b)
breadboards: 1

parts:
  DHT1 = DHT22 Humidity and Temperature Sensor
  microSD1 = MicroSD Breakout
  R1 = Resistor [tolerance=±5% resistance=10k package=THT]

nets:
  VDD: DHT1.VDD, microSD1.5V, R1.Pin_0
  N1: DHT1.DATA, R1.Pin_1
  GND: DHT1.GND, microSD1.GND

custom parts:
  MicroSD Breakout: 5V-ready microSD Breakout with Level Shifter
